// Logisim project alu.circ as structural Verilog: 1 circuit, main circuit main
module main (
  input  in_1,
  input  in_2,
  input  in_3,
  input  in_4,
  input  in_5,
  input  in_6,
  input  in_7,
  input  in_8,
  input  in_9,
  input  in_10,
  input  in_11,
  input  in_12,
  input  in_13,
  input  in_14,
  input  in_15,
  input  in_16,
  input  in_17,
  input  in_18,
  input  in_19
);

  wire _1s_place, _2s_place, _4s_place, _8s_place, _16s_place, _32s_place, _64s_place, _128s_place, A1_out,
       A2_out, A3_out, A4_out, A5_out, A6_out, A7_out, A8_out, add_or_subtract_out, adder_1_to_adder_2,
       adder_2_to_adder_3, adder_3_to_adder_4, adder_5_to_adder_6, adder_6_to_adder_7, adder_7_to_adder_8,
       and_1_out, and_2_out, and_3_out, and_4_out, and_5_out, and_6_out, and_7_out, and_8_out, and_9_out,
       and_10_out, and_11_out, and_12_out, and_13_out, and_14_out, and_15_out, and_16_out, and_17_out,
       and_18_out, and_19_out, and_20_out, and_21_out, and_22_out, and_23_out, and_24_out, and_29_out,
       and_30_out, and_31_out, and_32_out, and_33_out, and_34_out, and_35_out, and_36_out, and_37_out,
       and_38_out, and_39_out, and_40_out, and_41_out, and_42_out, and_43_out, and_44_out, and_49_out,
       and_50_out, and_51_out, and_52_out, and_53_out, and_54_out, and_55_out, and_56_out, and_62_out,
       and_68_out, and_69_out, B1_out, B2_out, B3_out, B4_out, B5_out, B6_out, B7_out, B8_out, carry_out,
       carry_out_to_inverter, not_1_out, not_2_out, not_3_out, not_4_out, not_5_out, not_6_out, not_7_out,
       not_8_out, not_9_out, not_10_out, not_11_out, not_12_out, not_13_out, not_14_out, not_15_out,
       not_16_out, not_17_out, not_18_out, not_19_out, not_20_out, not_21_out, not_22_out, not_23_out,
       not_24_out, not_25_out, not_26_out, not_27_out, not_28_out, or_12_out, run_alu_out,
       tristate_A_to_adder_1, tristate_A_to_adder_2, tristate_A_to_adder_3, tristate_A_to_adder_4,
       tristate_A_to_adder_5, tristate_A_to_adder_6, tristate_A_to_adder_7, tristate_A_to_adder_8,
       tristate_B_to_adder_1, tristate_B_to_adder_2, tristate_B_to_adder_3, tristate_B_to_adder_4,
       tristate_B_to_adder_5, tristate_B_to_adder_6, tristate_B_to_adder_7, tristate_B_to_adder_8, xor_1_out,
       xor_3_out, xor_5_out, xor_7_out, xor_9_out, xor_11_out, xor_13_out, xor_15_out;

  not not_1 (not_1_out, in_17);
  not not_2 (not_2_out, in_17);
  not not_3 (not_3_out, in_17);
  not not_4 (not_4_out, in_17);
  not not_5 (not_5_out, in_17);
  not not_6 (not_6_out, in_17);
  not not_7 (not_7_out, in_17);
  not not_8 (not_8_out, in_17);
  and and_1 (and_1_out, in_18, tristate_A_to_adder_1);
  xor xor_1 (xor_1_out, in_18, tristate_A_to_adder_1);
  and and_2 (and_2_out, xor_1_out, tristate_B_to_adder_1);
  xor xor_2 (_1s_place, xor_1_out, tristate_B_to_adder_1);
  and and_3 (and_3_out, adder_1_to_adder_2, tristate_A_to_adder_2);
  xor xor_3 (xor_3_out, adder_1_to_adder_2, tristate_A_to_adder_2);
  and and_4 (and_4_out, xor_3_out, tristate_B_to_adder_2);
  xor xor_4 (_2s_place, xor_3_out, tristate_B_to_adder_2);
  and and_5 (and_5_out, adder_2_to_adder_3, tristate_A_to_adder_3);
  xor xor_5 (xor_5_out, adder_2_to_adder_3, tristate_A_to_adder_3);
  and and_6 (and_6_out, xor_5_out, tristate_B_to_adder_3);
  xor xor_6 (_4s_place, xor_5_out, tristate_B_to_adder_3);
  and and_7 (and_7_out, adder_3_to_adder_4, tristate_A_to_adder_4);
  xor xor_7 (xor_7_out, adder_3_to_adder_4, tristate_A_to_adder_4);
  and and_8 (and_8_out, xor_7_out, tristate_B_to_adder_4);
  xor xor_8 (_8s_place, xor_7_out, tristate_B_to_adder_4);
  and and_9 (and_9_out, _1s_place, in_17);
  or or_1 (A1_out, and_9_out, and_10_out);
  and and_10 (and_10_out, not_1_out, in_8);
  and and_11 (and_11_out, _2s_place, in_17);
  or or_2 (A2_out, and_11_out, and_12_out);
  and and_12 (and_12_out, not_2_out, in_7);
  and and_13 (and_13_out, _4s_place, in_17);
  or or_3 (A3_out, and_13_out, and_14_out);
  and and_14 (and_14_out, not_3_out, in_6);
  and and_15 (and_15_out, _8s_place, in_17);
  or or_4 (A4_out, and_15_out, and_16_out);
  and and_16 (and_16_out, not_4_out, in_5);
  and and_17 (and_17_out, _16s_place, in_17);
  or or_5 (A5_out, and_17_out, and_18_out);
  and and_18 (and_18_out, not_5_out, in_4);
  and and_19 (and_19_out, _32s_place, in_17);
  or or_6 (A6_out, and_19_out, and_20_out);
  and and_20 (and_20_out, not_6_out, in_3);
  and and_21 (and_21_out, _64s_place, in_17);
  or or_7 (A7_out, and_21_out, and_22_out);
  and and_22 (and_22_out, not_7_out, in_2);
  and and_23 (and_23_out, _128s_place, in_17);
  or or_8 (A8_out, and_23_out, and_24_out);
  and and_24 (and_24_out, not_8_out, in_1);
  and and_25 (tristate_A_to_adder_4, in_17, in_5);
  and and_26 (tristate_A_to_adder_8, in_17, in_1);
  and and_27 (tristate_B_to_adder_4, in_17, B4_out);
  and and_28 (tristate_B_to_adder_8, in_17, B8_out);
  or or_9 (adder_1_to_adder_2, and_1_out, and_2_out);
  or or_10 (adder_2_to_adder_3, and_3_out, and_4_out);
  or or_11 (adder_3_to_adder_4, and_5_out, and_6_out);
  or or_12 (or_12_out, and_7_out, and_8_out);
  not not_9 (not_9_out, in_16);
  not not_10 (not_10_out, in_18);
  not not_11 (not_11_out, in_15);
  not not_12 (not_12_out, in_18);
  not not_13 (not_13_out, in_14);
  not not_14 (not_14_out, in_18);
  not not_15 (not_15_out, in_13);
  not not_16 (not_16_out, in_18);
  not not_17 (not_17_out, in_12);
  not not_18 (not_18_out, in_18);
  not not_19 (not_19_out, in_11);
  not not_20 (not_20_out, in_18);
  not not_21 (not_21_out, in_10);
  not not_22 (not_22_out, in_18);
  not not_23 (not_23_out, in_9);
  not not_24 (not_24_out, in_18);
  and and_29 (and_29_out, not_9_out, in_18);
  or or_13 (B1_out, and_29_out, and_30_out);
  and and_30 (and_30_out, not_10_out, in_16);
  and and_31 (and_31_out, not_11_out, in_18);
  or or_14 (B2_out, and_31_out, and_32_out);
  and and_32 (and_32_out, not_12_out, in_15);
  and and_33 (and_33_out, not_13_out, in_18);
  or or_15 (B3_out, and_33_out, and_34_out);
  and and_34 (and_34_out, not_14_out, in_14);
  and and_35 (and_35_out, not_15_out, in_18);
  or or_16 (B4_out, and_35_out, and_36_out);
  and and_36 (and_36_out, not_16_out, in_13);
  and and_37 (and_37_out, not_17_out, in_18);
  or or_17 (B5_out, and_37_out, and_38_out);
  and and_38 (and_38_out, not_18_out, in_12);
  and and_39 (and_39_out, not_19_out, in_18);
  or or_18 (B6_out, and_39_out, and_40_out);
  and and_40 (and_40_out, not_20_out, in_11);
  and and_41 (and_41_out, not_21_out, in_18);
  or or_19 (B7_out, and_41_out, and_42_out);
  and and_42 (and_42_out, not_22_out, in_10);
  and and_43 (and_43_out, not_23_out, in_18);
  or or_20 (B8_out, and_43_out, and_44_out);
  and and_44 (and_44_out, not_24_out, in_9);
  and and_45 (tristate_A_to_adder_3, in_17, in_6);
  and and_46 (tristate_A_to_adder_7, in_17, in_2);
  and and_47 (tristate_B_to_adder_3, in_17, B3_out);
  and and_48 (tristate_B_to_adder_7, in_17, B7_out);
  and and_49 (and_49_out, or_12_out, tristate_A_to_adder_5);
  xor xor_9 (xor_9_out, or_12_out, tristate_A_to_adder_5);
  and and_50 (and_50_out, xor_9_out, tristate_B_to_adder_5);
  xor xor_10 (_16s_place, xor_9_out, tristate_B_to_adder_5);
  and and_51 (and_51_out, adder_5_to_adder_6, tristate_A_to_adder_6);
  xor xor_11 (xor_11_out, adder_5_to_adder_6, tristate_A_to_adder_6);
  and and_52 (and_52_out, xor_11_out, tristate_B_to_adder_6);
  xor xor_12 (_32s_place, xor_11_out, tristate_B_to_adder_6);
  and and_53 (and_53_out, adder_6_to_adder_7, tristate_A_to_adder_7);
  xor xor_13 (xor_13_out, adder_6_to_adder_7, tristate_A_to_adder_7);
  and and_54 (and_54_out, xor_13_out, tristate_B_to_adder_7);
  xor xor_14 (_64s_place, xor_13_out, tristate_B_to_adder_7);
  and and_55 (and_55_out, adder_7_to_adder_8, tristate_A_to_adder_8);
  xor xor_15 (xor_15_out, adder_7_to_adder_8, tristate_A_to_adder_8);
  and and_56 (and_56_out, xor_15_out, tristate_B_to_adder_8);
  xor xor_16 (_128s_place, xor_15_out, tristate_B_to_adder_8);
  or or_21 (adder_5_to_adder_6, and_49_out, and_50_out);
  or or_22 (adder_6_to_adder_7, and_51_out, and_52_out);
  or or_23 (adder_7_to_adder_8, and_53_out, and_54_out);
  or or_24 (carry_out_to_inverter, and_55_out, and_56_out);
  and and_57 (run_alu_out, in_17, not_25_out);
  not not_25 (not_25_out, in_17);
  and and_58 (tristate_A_to_adder_2, in_17, in_7);
  and and_59 (tristate_A_to_adder_6, in_17, in_3);
  and and_60 (tristate_B_to_adder_2, in_17, B2_out);
  and and_61 (tristate_B_to_adder_6, in_17, B6_out);
  LED led_1 (.in(run_alu_out));
  LED led_2 (.in(add_or_subtract_out));
  LED led_3 (.in(carry_out));
  LED led_4 (.in(A8_out));
  LED led_5 (.in(A7_out));
  LED led_6 (.in(A6_out));
  LED led_7 (.in(A5_out));
  LED led_8 (.in(A4_out));
  LED led_9 (.in(A3_out));
  LED led_10 (.in(A2_out));
  LED led_11 (.in(A1_out));
  LED led_12 (.in(B8_out));
  LED led_13 (.in(B7_out));
  LED led_14 (.in(B6_out));
  LED led_15 (.in(B5_out));
  LED led_16 (.in(B4_out));
  LED led_17 (.in(B3_out));
  LED led_18 (.in(B2_out));
  LED led_19 (.in(B1_out));
  not not_26 (not_26_out, in_18);
  and and_62 (and_62_out, carry_out_to_inverter, not_27_out);
  not not_27 (not_27_out, carry_out_to_inverter);
  not not_28 (not_28_out, in_18);
  and and_63 (tristate_A_to_adder_1, in_17, in_8);
  and and_64 (tristate_A_to_adder_5, in_17, in_4);
  and and_65 (tristate_B_to_adder_1, in_17, B1_out);
  and and_66 (tristate_B_to_adder_5, in_17, B5_out);
  and and_67 (add_or_subtract_out, in_18, not_26_out);
  and and_68 (and_68_out, and_62_out, in_18);
  or or_25 (carry_out, and_68_out, and_69_out);
  and and_69 (and_69_out, not_28_out, carry_out_to_inverter);

  // Other names for the same wires on the sheet: A1_to_tristate = in_8; A2_to_tristate = in_7; A3_to_tristate = in_6;
  //   A4_to_tristate = in_5; A5_to_tristate = in_4; A6_to_tristate = in_3; A7_to_tristate = in_2;
  //   A8_to_tristate = in_1; add_or_subtract = in_18; B1_inverter = in_16; B1_to_tristate = B1_out;
  //   B2_inverter = in_15; B2_to_tristate = B2_out; B3_inverter = in_14; B3_to_tristate = B3_out; B4_inverter = in_13;
  //   B4_to_tristate = B4_out; B5_inverter = in_12; B5_to_tristate = B5_out; B6_inverter = in_11;
  //   B6_to_tristate = B6_out; B7_inverter = in_10; B7_to_tristate = B7_out; B8_inverter = in_9;
  //   B8_to_tristate = B8_out; initial_carry_out = in_19; run_alu = in_17

  // Notes on the sheet:
  //   to second 4bit adder
  //   carry in
endmodule
